// Logisim project 1.circ as structural Verilog: 7 circuits, main circuit main
module main (
  input  in_1,
  output [5:0] opcode,
  output [5:0] funct,
  output [31:0] out_4
);

  wire ALUSrc, clk, extop, MenToReg, MenWrite, npc_sel, or_1_out, RegDst, ReWrite, zero;
  wire [2:0] controller_1_aluctr;
  wire [4:0] multiplexer_1_out;
  wire [31:0] alu_1_out, dm_1_out, ext_1_out_3, multiplexer_2_out, multiplexer_3_out, refile_1_busa,
       refile_1_busb;

  Clock clock_1 (.out(clk));
  PC pc_1 (.ifBeq(npc_sel), .zero(zero), .clk(clk), .out_5({opcode, out_4[25:6], funct}), .reset(in_1));
  Controller controller_1 (
    .funct(funct), .opcode(opcode), .RegDst(RegDst), .ALUSrc(ALUSrc), .MemtoReg(MenToReg),
    .RegWrite(ReWrite), .MemWrite(MenWrite), .nPCsel(npc_sel), .ExtOp(extop), .ALUctr(controller_1_aluctr));
  Multiplexer #(.width(5), .enable("false")) multiplexer_1 (
    .in0(out_4[20:16]), .in1(out_4[15:11]), .out(multiplexer_1_out), .sel(RegDst));
  REfile refile_1 (
    .reset(in_1), .RegWrite(ReWrite), .A1(multiplexer_1_out), .A2(out_4[20:16]), .A3(out_4[25:21]),
    .IN(multiplexer_3_out), .busA(refile_1_busa), .busB(refile_1_busb));
  Multiplexer #(.width(32), .enable("false")) multiplexer_2 (
    .in0(refile_1_busb), .in1(ext_1_out_3), .out(multiplexer_2_out), .sel(ALUSrc));
  EXT ext_1 (.in_1({out_4[15:6], funct}), .Extop(extop), .out_3(ext_1_out_3));
  Multiplexer #(.width(32), .enable("false")) multiplexer_3 (
    .in0(alu_1_out), .in1(dm_1_out), .out(multiplexer_3_out), .sel(MenToReg));
  ALU alu_1 (.A(refile_1_busa), .B(multiplexer_2_out), .ALUctr(controller_1_aluctr), .OUT(alu_1_out));
  DM dm_1 (.A(alu_1_out[6:2]), .D(refile_1_busb), .Memwrite(MenWrite), .CLK(clk), .reset(in_1), .out(dm_1_out));
  or or_1 (or_1_out, alu_1_out[31], alu_1_out[30], alu_1_out[29], alu_1_out[28], alu_1_out[27], alu_1_out[26], alu_1_out[25], alu_1_out[24], alu_1_out[23], alu_1_out[22], alu_1_out[21], alu_1_out[20], alu_1_out[19], alu_1_out[18], alu_1_out[17], alu_1_out[16], alu_1_out[14], alu_1_out[13], alu_1_out[12], alu_1_out[11], alu_1_out[10], alu_1_out[9], alu_1_out[8], alu_1_out[7], alu_1_out[6], alu_1_out[5], alu_1_out[4], alu_1_out[3], alu_1_out[2], alu_1_out[1], alu_1_out[0], alu_1_out[15]);
  not not_1 (zero, or_1_out);

  assign {out_4[31:26], out_4[5:0]} = {opcode, funct};

  // Other names for the same wires on the sheet: imm16[15:0] = {out_4[15:6], funct}; Rd[4:0] = out_4[15:11];
  //   Rt[4:0] = out_4[20:16]; Rs[4:0] = out_4[25:21]; reset = in_1
endmodule

module ALU (
  input  [31:0] A,
  input  [31:0] B,
  input  [2:0] ALUctr,
  output [31:0] OUT
);

  wire [31:0] adder_1_out, or_1_out, subtractor_1_out;

  Adder #(.width(32)) adder_1 (.a(A), .b(B), .out(adder_1_out));  // open: cin, cout
  Subtractor #(.width(32)) subtractor_1 (.a(A), .b(B), .out(subtractor_1_out));  // open: bin, bout
  assign or_1_out = A | B;  // OR_Gate or_1, 32 bits wide
  Multiplexer #(.select(3), .width(32), .enable("false")) multiplexer_1 (
    .in0(B), .in1(adder_1_out), .in2(subtractor_1_out), .in3(or_1_out), .out(OUT), .sel(ALUctr));  // open: in4, in5, in6, in7
endmodule

// refile
module REfile (
  input  reset,
  input  RegWrite,
  input  [4:0] A1,
  input  [4:0] A2,
  input  [4:0] A3,
  input  [31:0] IN,
  output [31:0] busA,
  output [31:0] busB
);

  wire Clk_out, demultiplexer_1_out1, demultiplexer_1_out2, demultiplexer_1_out3, demultiplexer_1_out4,
       demultiplexer_1_out5, demultiplexer_1_out6, demultiplexer_1_out7, demultiplexer_1_out8,
       demultiplexer_1_out9, demultiplexer_1_out10, demultiplexer_1_out11, demultiplexer_1_out12,
       demultiplexer_1_out13, demultiplexer_1_out14, demultiplexer_1_out15, demultiplexer_1_out16,
       demultiplexer_1_out17, demultiplexer_1_out18, demultiplexer_1_out19, demultiplexer_1_out20,
       demultiplexer_1_out21, demultiplexer_1_out22, demultiplexer_1_out23, demultiplexer_1_out24,
       demultiplexer_1_out25, demultiplexer_1_out26, demultiplexer_1_out27, demultiplexer_1_out28,
       demultiplexer_1_out29, demultiplexer_1_out30, demultiplexer_1_out31;
  wire [31:0] _0, _1, _2, _3, _4, _5, _6, _7, _8, _9, _10, _11, _12, _13, _14, _15, _16, _17, _18, _19, _20,
       _21, _22, _23, _24, _25, _26, _27, _28, _29, _30, _31;

  Demultiplexer #(.select(5), .enable("false")) demultiplexer_1 (
    .out1(demultiplexer_1_out1), .out2(demultiplexer_1_out2), .out3(demultiplexer_1_out3),
    .out4(demultiplexer_1_out4), .out5(demultiplexer_1_out5), .out6(demultiplexer_1_out6),
    .out7(demultiplexer_1_out7), .out8(demultiplexer_1_out8), .out9(demultiplexer_1_out9),
    .out10(demultiplexer_1_out10), .out11(demultiplexer_1_out11), .out12(demultiplexer_1_out12),
    .out13(demultiplexer_1_out13), .out14(demultiplexer_1_out14), .out15(demultiplexer_1_out15),
    .out16(demultiplexer_1_out16), .out17(demultiplexer_1_out17), .out18(demultiplexer_1_out18),
    .out19(demultiplexer_1_out19), .out20(demultiplexer_1_out20), .out21(demultiplexer_1_out21),
    .out22(demultiplexer_1_out22), .out23(demultiplexer_1_out23), .out24(demultiplexer_1_out24),
    .out25(demultiplexer_1_out25), .out26(demultiplexer_1_out26), .out27(demultiplexer_1_out27),
    .out28(demultiplexer_1_out28), .out29(demultiplexer_1_out29), .out30(demultiplexer_1_out30),
    .out31(demultiplexer_1_out31), .in(RegWrite), .sel(A1));  // open: out0
  Clock Clk (.out(Clk_out));
  Register #(.width(32)) register_1 (.Q(_0), .clk(Clk_out), .clr(reset));  // open: D, en
  Register #(.width(32)) register_2 (.D(IN), .en(demultiplexer_1_out1), .Q(_1), .clk(Clk_out), .clr(reset));
  Register #(.width(32)) register_3 (.D(IN), .en(demultiplexer_1_out2), .Q(_2), .clk(Clk_out), .clr(reset));
  Register #(.width(32)) register_4 (.D(IN), .en(demultiplexer_1_out3), .Q(_3), .clk(Clk_out), .clr(reset));
  Register #(.width(32)) register_5 (.D(IN), .en(demultiplexer_1_out4), .Q(_4), .clk(Clk_out), .clr(reset));
  Register #(.width(32)) register_6 (.D(IN), .en(demultiplexer_1_out5), .Q(_5), .clk(Clk_out), .clr(reset));
  Register #(.width(32)) register_7 (.D(IN), .en(demultiplexer_1_out6), .Q(_6), .clk(Clk_out), .clr(reset));
  Register #(.width(32)) register_8 (.D(IN), .en(demultiplexer_1_out7), .Q(_7), .clk(Clk_out), .clr(reset));
  Register #(.width(32)) register_9 (.D(IN), .en(demultiplexer_1_out8), .Q(_8), .clk(Clk_out), .clr(reset));
  Register #(.width(32)) register_10 (.D(IN), .en(demultiplexer_1_out9), .Q(_9), .clk(Clk_out), .clr(reset));
  Register #(.width(32)) register_11 (.D(IN), .en(demultiplexer_1_out10), .Q(_10), .clk(Clk_out), .clr(reset));
  Register #(.width(32)) register_12 (.D(IN), .en(demultiplexer_1_out11), .Q(_11), .clk(Clk_out), .clr(reset));
  Register #(.width(32)) register_13 (.D(IN), .en(demultiplexer_1_out12), .Q(_12), .clk(Clk_out), .clr(reset));
  Register #(.width(32)) register_14 (.D(IN), .en(demultiplexer_1_out13), .Q(_13), .clk(Clk_out), .clr(reset));
  Register #(.width(32)) register_15 (.D(IN), .en(demultiplexer_1_out14), .Q(_14), .clk(Clk_out), .clr(reset));
  Register #(.width(32)) register_16 (.D(IN), .en(demultiplexer_1_out15), .Q(_15), .clk(Clk_out), .clr(reset));
  Register #(.width(32)) register_17 (.D(IN), .en(demultiplexer_1_out16), .Q(_16), .clk(Clk_out), .clr(reset));
  Register #(.width(32)) register_18 (.D(IN), .en(demultiplexer_1_out17), .Q(_17), .clk(Clk_out), .clr(reset));
  Register #(.width(32)) register_19 (.D(IN), .en(demultiplexer_1_out18), .Q(_18), .clk(Clk_out), .clr(reset));
  Register #(.width(32)) register_20 (.D(IN), .en(demultiplexer_1_out19), .Q(_19), .clk(Clk_out), .clr(reset));
  Register #(.width(32)) register_21 (.D(IN), .en(demultiplexer_1_out20), .Q(_20), .clk(Clk_out), .clr(reset));
  Register #(.width(32)) register_22 (.D(IN), .en(demultiplexer_1_out21), .Q(_21), .clk(Clk_out), .clr(reset));
  Register #(.width(32)) register_23 (.D(IN), .en(demultiplexer_1_out22), .Q(_22), .clk(Clk_out), .clr(reset));
  Register #(.width(32)) register_24 (.D(IN), .en(demultiplexer_1_out23), .Q(_23), .clk(Clk_out), .clr(reset));
  Register #(.width(32)) register_25 (.D(IN), .en(demultiplexer_1_out24), .Q(_24), .clk(Clk_out), .clr(reset));
  Register #(.width(32)) register_26 (.D(IN), .en(demultiplexer_1_out25), .Q(_25), .clk(Clk_out), .clr(reset));
  Register #(.width(32)) register_27 (.D(IN), .en(demultiplexer_1_out26), .Q(_26), .clk(Clk_out), .clr(reset));
  Register #(.width(32)) register_28 (.D(IN), .en(demultiplexer_1_out27), .Q(_27), .clk(Clk_out), .clr(reset));
  Register #(.width(32)) register_29 (.D(IN), .en(demultiplexer_1_out28), .Q(_28), .clk(Clk_out), .clr(reset));
  Register #(.width(32)) register_30 (.D(IN), .en(demultiplexer_1_out29), .Q(_29), .clk(Clk_out), .clr(reset));
  Register #(.width(32)) register_31 (.D(IN), .en(demultiplexer_1_out30), .Q(_30), .clk(Clk_out), .clr(reset));
  Register #(.width(32)) register_32 (.D(IN), .en(demultiplexer_1_out31), .Q(_31), .clk(Clk_out), .clr(reset));
  Multiplexer #(.select(5), .width(32), .enable("false")) multiplexer_1 (
    .in0(_0), .in1(_1), .in2(_2), .in3(_3), .in4(_4), .in5(_5), .in6(_6), .in7(_7), .in8(_8), .in9(_9),
    .in10(_10), .in11(_11), .in12(_12), .in13(_13), .in14(_14), .in15(_15), .in16(_16), .in17(_17),
    .in18(_18), .in19(_19), .in20(_20), .in21(_21), .in22(_22), .in23(_23), .in24(_24), .in25(_25),
    .in26(_26), .in27(_27), .in28(_28), .in29(_29), .in30(_30), .in31(_31), .out(busA), .sel(A2));
  Multiplexer #(.select(5), .width(32), .enable("false")) multiplexer_2 (
    .in0(_0), .in1(_1), .in2(_2), .in3(_3), .in4(_4), .in5(_5), .in6(_6), .in7(_7), .in8(_8), .in9(_9),
    .in10(_10), .in11(_11), .in12(_12), .in13(_13), .in14(_14), .in15(_15), .in16(_16), .in17(_17),
    .in18(_18), .in19(_19), .in20(_20), .in21(_21), .in22(_22), .in23(_23), .in24(_24), .in25(_25),
    .in26(_26), .in27(_27), .in28(_28), .in29(_29), .in30(_30), .in31(_31), .out(busB), .sel(A3));
endmodule

// EXtender
module EXT (
  input  [15:0] in_1,
  input  Extop,
  output [31:0] out_3
);

  wire [31:0] bit_extender_1_out;

  assign bit_extender_1_out = {{16{1'b0}}, in_1};  // Bit_Extender bit_extender_1
  Multiplexer #(.width(32), .enable("false")) multiplexer_1 (
    .in0(bit_extender_1_out), .in1({in_1, {16{1'b0}}}), .out(out_3), .sel(Extop));
endmodule

module PC (
  input  ifBeq,
  input  zero,
  input  clk,
  input  reset,
  output [31:0] out_5
);

  wire [29:0] beq_pc, multiplexer_1_out, PC, PC_1;
  wire [31:0] bit_extender_1_out;
  wire [31:30] adder_1_out, adder_2_out;

  Adder #(.width(32)) adder_1 (.a({2'b00, PC}), .b(32'h1), .out({adder_1_out, PC_1}));  // open: cin, cout
  assign bit_extender_1_out = {{16{1'b0}}, out_5[15:0]};  // Bit_Extender bit_extender_1
  Adder #(.width(32)) adder_2 (
    .a(bit_extender_1_out), .b({2'b00, PC_1}), .out({adder_2_out, beq_pc}));  // open: cin, cout
  Multiplexer #(.select(2), .width(30), .enable("false")) multiplexer_1 (
    .in0(PC_1), .in1(PC_1), .in2(PC_1), .in3(beq_pc), .out(multiplexer_1_out), .sel({zero, ifBeq}));
  Register #(.width(30)) u_pc (.D(multiplexer_1_out), .Q(PC), .clk(clk), .clr(reset));  // open: en
  RAM #(.addrWidth(5), .dataWidth(32)) ram_1 (.addr(PC[4:0]), .data(out_5));  // open: sel, clk, ld, clr

  // Other names for the same wires on the sheet: inst[31:0] = out_5; Sel[1:0] = {zero, ifBeq}

  // Notes on the sheet:
  //   IM
endmodule

module DM (
  input  [4:0] A,
  input  [31:0] D,
  input  Memwrite,
  input  CLK,
  input  reset,
  output [31:0] out
);

  RAM #(.addrWidth(5), .dataWidth(32), .bus("separate")) ram_1 (
    .addr(A), .din(D), .data(out), .str(Memwrite), .clk(CLK), .clr(reset));  // open: sel, ld
endmodule

module Controller (
  input  [5:0] funct,
  input  [5:0] opcode,
  output RegDst,
  output ALUSrc,
  output MemtoReg,
  output RegWrite,
  output MemWrite,
  output nPCsel,
  output ExtOp,
  output [2:0] ALUctr
);

  wire addu, subu;

  and and_1 (addu, funct[5], ~funct[4], ~funct[3], ~funct[2], ~funct[1], ~funct[0], ~opcode[5], ~opcode[4], ~opcode[3], ~opcode[2], ~opcode[1], ~opcode[0]);  // AND_Gate
  and and_2 (subu, funct[5], ~funct[4], ~funct[3], ~funct[2], funct[1], ~funct[0], ~opcode[5], ~opcode[4], ~opcode[3], ~opcode[2], ~opcode[1], ~opcode[0]);  // AND_Gate
  and and_3 (ALUctr[1], ~opcode[5], ~opcode[4], opcode[3], opcode[2], ~opcode[1], opcode[0]);  // AND_Gate
  and and_4 (MemtoReg, opcode[5], ~opcode[4], ~opcode[3], ~opcode[2], opcode[1], opcode[0]);  // AND_Gate
  and and_5 (MemWrite, opcode[5], ~opcode[4], opcode[3], ~opcode[2], opcode[1], opcode[0]);  // AND_Gate
  and and_6 (nPCsel, ~opcode[5], ~opcode[4], ~opcode[3], opcode[2], ~opcode[1], ~opcode[0]);  // AND_Gate
  or or_1 (RegDst, addu, subu);
  or or_2 (ALUSrc, ALUctr[1], MemtoReg, MemWrite);
  or or_3 (RegWrite, addu, subu, ALUctr[1], MemtoReg);
  or or_4 (ExtOp, MemWrite, MemtoReg);
  and and_7 (ALUctr[0], ~nPCsel, ~subu);  // AND_Gate

  assign ALUctr[2] = 1'b0;

  // Other names for the same wires on the sheet: ori = ALUctr[1]; beq = nPCsel; lw = MemtoReg; sw = MemWrite
endmodule
