// Logisim project alu.circ as structural Verilog: 1 circuit, main circuit alu
module alu (
  input  [31:0] A,
  input  [31:0] B,
  input  [3:0] ALUSel,
  output [31:0] Result,
  output [31:0] out_5
);

  wire comparator_1_lt, or_1_out, or_2_out, or_3_out, xor_2_out, xor_3_out;
  wire [31:0] add0, and1, div8, mul10, mulh14, mulhu11, multiplexer_2_out, multiplexer_3_out,
       multiplexer_4_out, multiplexer_5_out, multiplexer_6_out, multiplier_3_cout, multiplier_3_out,
       negator_1_out, negator_2_out, negator_3_out, negator_4_out, not_1_out, or2, remu9, sll6, slt7, sra5,
       srl4, sub12, xor3;

  or or_1 (or_1_out, B[5], B[6], B[7], B[8], B[9], B[10], B[11], B[12], B[13], B[14], B[15], B[16], B[17], B[18], B[19], B[20], B[21], B[22], B[23], B[24], B[25], B[26], B[27], B[28], B[29], B[30], B[31]);
  or or_2 (or_2_out, B[5], B[6], B[7], B[8], B[9], B[10], B[11], B[12], B[13], B[14], B[15], B[16], B[17], B[18], B[19], B[20], B[21], B[22], B[23], B[24], B[25], B[26], B[27], B[28], B[29], B[30], B[31]);
  or or_3 (or_3_out, B[5], B[6], B[7], B[8], B[9], B[10], B[11], B[12], B[13], B[14], B[15], B[16], B[17], B[18], B[19], B[20], B[21], B[22], B[23], B[24], B[25], B[26], B[27], B[28], B[29], B[30], B[31]);
  Comparator #(.width(32)) comparator_1 (.a(A), .b(B), .lt(comparator_1_lt));  // open: gt, eq
  Negator #(.width(32)) negator_1 (.in(A), .out(negator_1_out));
  Negator #(.width(32)) negator_2 (.in(B), .out(negator_2_out));
  Adder #(.width(32)) adder_1 (.a(A), .b(B), .out(add0));  // open: cin, cout
  assign and1 = A & B;  // AND_Gate and_1, 32 bits wide
  assign or2 = A | B;  // OR_Gate or_4, 32 bits wide
  assign xor3 = A ^ B;  // XOR_Gate xor_1, 32 bits wide
  Shifter #(.width(32), .shift("lr")) shifter_1 (.in(A), .\dist (B[4:0]), .out(srl4));
  Multiplexer #(.width(32), .enable("false")) multiplexer_1 (.in1({32{1'b0}}), .sel(or_1_out));  // open: in0, out
  Shifter #(.width(32), .shift("ar")) shifter_2 (.in(A), .\dist (B[4:0]), .out(sra5));
  Multiplexer #(.width(32), .enable("false")) multiplexer_2 (
    .in1({32{1'b0}}), .out(multiplexer_2_out), .sel(or_2_out));  // open: in0
  Shifter #(.width(32)) shifter_3 (.in(A), .\dist (B[4:0]), .out(sll6));
  Multiplexer #(.width(32), .enable("false")) multiplexer_3 (
    .in1({32{1'b0}}), .out(multiplexer_3_out), .sel(or_3_out));  // open: in0
  assign slt7 = {{31{1'b0}}, comparator_1_lt};  // Bit_Extender bit_extender_1
  Divider #(.width(32)) divider_1 (.a(A), .b(B), .out(div8));  // open: upper, rem
  Divider #(.width(32)) divider_2 (.a(A), .b(B), .rem(remu9));  // open: out, upper
  Multiplier #(.width(32)) multiplier_1 (.a(A), .b(B), .out(mul10));  // open: cin, cout
  Multiplier #(.width(32)) multiplier_2 (.a(A), .b(B), .cout(mulhu11));  // open: out, cin
  Subtractor #(.width(32)) subtractor_1 (.a(A), .b(B), .out(sub12));  // open: bin, bout
  Multiplexer #(.width(32), .enable("false")) multiplexer_4 (
    .in0(A), .in1(negator_1_out), .out(multiplexer_4_out), .sel(A[31]));
  Multiplexer #(.width(32), .enable("false")) multiplexer_5 (
    .in0(B), .in1(negator_2_out), .out(multiplexer_5_out), .sel(B[31]));
  Multiplier #(.width(32)) multiplier_3 (
    .a(multiplexer_4_out), .b(multiplexer_5_out), .out(multiplier_3_out), .cout(multiplier_3_cout));  // open: cin
  xor xor_2 (xor_2_out, A[31], B[31]);
  Negator #(.width(32)) negator_3 (.in(multiplier_3_out), .out(negator_3_out));
  Negator #(.width(32)) negator_4 (.in(multiplier_3_cout), .out(negator_4_out));
  assign not_1_out = ~multiplier_3_cout;  // NOT_Gate not_1, 32 bits wide
  Multiplexer #(.width(32), .enable("false")) multiplexer_6 (
    .in0(negator_4_out), .in1(not_1_out), .out(multiplexer_6_out), .sel(xor_3_out));
  xor xor_3 (xor_3_out, multiplier_3_out[31], negator_3_out[31]);
  Multiplexer #(.width(32), .enable("false")) multiplexer_7 (
    .in0(multiplier_3_cout), .in1(multiplexer_6_out), .out(mulh14), .sel(xor_2_out));
  Multiplexer #(.select(4), .width(32), .enable("false")) multiplexer_8 (
    .in0(add0), .in1(and1), .in2(or2), .in3(xor3), .in4(srl4), .in5(sra5), .in6(sll6), .in7(slt7),
    .in8(div8), .in9(remu9), .in10(mul10), .in11(mulhu11), .in12(sub12), .in13(B), .in14(mulh14),
    .out(Result), .sel(ALUSel));  // open: in15

  assign out_5 = A;

  // Other names for the same wires on the sheet: bsel13[31:0] = B

  // Notes on the sheet:
  //   INPUTS to your circuit
  //   DON'T CHANGE THE LOCATIONS OF THE INPUTS AND OUTPUTS!
  //   OUTPUT from your circuit
endmodule
