// Logisim project cpu.circ as structural Verilog: 4 circuits, main circuit main
module main (
  input  [31:0] INSTRUCTION,
  input  CLOCK,
  output [31:0] PROGRAM_COUNTER,
  output [31:0] ra,
  output [31:0] sp,
  output [31:0] t0,
  output [31:0] t1,
  output [31:0] t2,
  output [31:0] s0,
  output [31:0] s1,
  output [31:0] a0
);

  wire ALUSrc, comparator_1_eq, comparator_2_eq, jump, MemtoReg, MemWr, not_1_out, nPCsel, or_1_out,
       or_3_out, RegWr, zero;
  wire [1:0] lhb;
  wire [2:0] ExtOp, funct3;
  wire [3:0] ALUctr;
  wire [4:0] rd, rs1, rs2;
  wire [6:0] funct7, opcode;
  wire [31:0] adder_2_out, adder_3_out, and_1_out, and_2_out, Arithmetic_Logic_Unit_result, beq,
       bit_extender_1_out, bit_extender_2_out, DMEM_p5, imm, immediategenerator_1_b, immediategenerator_1_i,
       immediategenerator_1_j, immediategenerator_1_s, immediategenerator_1_u, J, load_1_out_3,
       multiplexer_1_out, multiplexer_3_out, multiplexer_5_out, multiplexer_6_out, multiplexer_7_out, PC,
       PC4, PROGRAM_COUNTER_delay, RegFile_read_data_2, rs1out, wb0;

  Register #(.width(32)) register_1 (.D(PC), .clk(CLOCK), .Q(PROGRAM_COUNTER));  // open: en, clr
  or or_1 (or_1_out, nPCsel, jump);
  Register #(.width(32)) register_2 (.D(PROGRAM_COUNTER), .clk(CLOCK), .Q(PROGRAM_COUNTER_delay));  // open: en, clr
  Comparator #(.width(7)) comparator_1 (.a(7'b1100111), .b(opcode), .eq(comparator_1_eq));  // open: gt, lt
  Comparator #(.width(7)) comparator_2 (.a(7'b1101111), .b(opcode), .eq(comparator_2_eq));  // open: gt, lt
  Register #(.width(32)) register_3 (
    .D(multiplexer_1_out), .en(1'b1), .clk(CLOCK), .Q({funct7, rs2, rs1, funct3, rd, opcode}));  // open: clr
  Multiplexer #(.width(32), .enable("false")) multiplexer_1 (
    .in0(INSTRUCTION), .in1(32'h13), .out(multiplexer_1_out), .sel(or_1_out));
  Adder #(.width(32)) adder_1 (.a(PROGRAM_COUNTER_delay), .b(32'h4), .out(wb0));  // open: cin, cout
  assign bit_extender_1_out = {{31{comparator_1_eq}}, comparator_1_eq};  // Bit_Extender bit_extender_1
  Adder #(.width(32)) adder_2 (.a(rs1out), .b(imm), .out(adder_2_out));  // open: cin, cout
  Adder #(.width(32)) adder_3 (.a(PROGRAM_COUNTER_delay), .b(imm), .out(adder_3_out));  // open: cin, cout
  assign bit_extender_2_out = {{31{comparator_2_eq}}, comparator_2_eq};  // Bit_Extender bit_extender_2
  assign and_1_out = bit_extender_1_out & adder_2_out;  // AND_Gate and_1, 32 bits wide
  assign and_2_out = adder_3_out & bit_extender_2_out;  // AND_Gate and_2, 32 bits wide
  assign J = and_1_out | and_2_out;  // OR_Gate or_2, 32 bits wide
  ImmediateGenerator immediategenerator_1 (
    .INSTRUCTION({funct7, rs2, rs1, funct3, rd, opcode}), .I(immediategenerator_1_i),
    .S(immediategenerator_1_s), .B(immediategenerator_1_b), .U(immediategenerator_1_u),
    .J(immediategenerator_1_j));
  Multiplexer #(.select(3), .width(32), .enable("false")) multiplexer_2 (
    .in0(immediategenerator_1_i), .in1(immediategenerator_1_s), .in2(immediategenerator_1_b),
    .in3(immediategenerator_1_u), .in4(immediategenerator_1_j), .out(imm), .sel(ExtOp));  // open: in5, in6, in7
  Multiplexer #(.width(32), .enable("false")) multiplexer_3 (
    .in0(PC4), .in1(beq), .out(multiplexer_3_out), .sel(nPCsel));
  Adder #(.width(32)) adder_4 (.a(PROGRAM_COUNTER), .b(32'h4), .out(PC4));  // open: cin, cout
  Multiplexer #(.width(32), .enable("false")) multiplexer_4 (.in0(multiplexer_3_out), .in1(J), .out(PC), .sel(jump));
  Adder #(.width(32)) adder_5 (.a(PROGRAM_COUNTER_delay), .b(imm), .out(beq));  // open: cin, cout
  regfile_main RegFile (
    .rs2(rs2), .rd(rd), .Read_Data_1(rs1out), .Read_Data_2(RegFile_read_data_2), .ra(ra), .sp(sp), .t0(t0),
    .t1(t1), .t2(t2), .s0(s0), .s1(s1), .a0(a0), .rs1(rs1), .Write_Data(multiplexer_6_out), .RegWEn(RegWr),
    .clk(CLOCK));
  load load_1 (.in_1(multiplexer_7_out), .in_2(lhb), .out_3(load_1_out_3));
  Multiplexer #(.width(32), .enable("false")) multiplexer_5 (
    .in0(RegFile_read_data_2), .in1(imm), .out(multiplexer_5_out), .sel(ALUSrc));
  Multiplexer #(.width(32), .enable("false")) multiplexer_6 (
    .in0(load_1_out_3), .in1(wb0), .out(multiplexer_6_out), .sel(jump));
  alu Arithmetic_Logic_Unit (
    .ALUSel(ALUctr), .B(multiplexer_5_out), .A(rs1out), .Result(Arithmetic_Logic_Unit_result));  // open: out_5
  ControlModule controlmodule_1 (
    .opcode(opcode), .func7(funct7), .func3(funct3), .zero(zero), .ALUsrc(ALUSrc), .MentoReg(MemtoReg),
    .RegWr(RegWr), .MenWr(MemWr), .ExtOp(ExtOp), .ALUctr(ALUctr), .nPCsel(nPCsel), .jump(jump), .lhb(lhb));
  Register #(.width(1)) register_4 (.D(not_1_out), .en(1'b1), .clk(CLOCK), .Q(zero));  // open: clr
  or or_3 (or_3_out, Arithmetic_Logic_Unit_result[31], Arithmetic_Logic_Unit_result[30], Arithmetic_Logic_Unit_result[29], Arithmetic_Logic_Unit_result[28], Arithmetic_Logic_Unit_result[27], Arithmetic_Logic_Unit_result[26], Arithmetic_Logic_Unit_result[25], Arithmetic_Logic_Unit_result[24], Arithmetic_Logic_Unit_result[23], Arithmetic_Logic_Unit_result[22], Arithmetic_Logic_Unit_result[21], Arithmetic_Logic_Unit_result[20], Arithmetic_Logic_Unit_result[19], Arithmetic_Logic_Unit_result[18], Arithmetic_Logic_Unit_result[17], Arithmetic_Logic_Unit_result[16], Arithmetic_Logic_Unit_result[14], Arithmetic_Logic_Unit_result[13], Arithmetic_Logic_Unit_result[12], Arithmetic_Logic_Unit_result[11], Arithmetic_Logic_Unit_result[10], Arithmetic_Logic_Unit_result[9], Arithmetic_Logic_Unit_result[8], Arithmetic_Logic_Unit_result[7], Arithmetic_Logic_Unit_result[6], Arithmetic_Logic_Unit_result[5], Arithmetic_Logic_Unit_result[4], Arithmetic_Logic_Unit_result[3], Arithmetic_Logic_Unit_result[2], Arithmetic_Logic_Unit_result[1], Arithmetic_Logic_Unit_result[0], Arithmetic_Logic_Unit_result[15]);
  not not_1 (not_1_out, or_3_out);
  // mem_main DMEM: pin names not known; wires that end beside it: Arithmetic_Logic_Unit_result, RegFile_read_data_2, CLOCK, MemWr, DMEM_p5
  Multiplexer #(.width(32), .enable("false")) multiplexer_7 (
    .in0(Arithmetic_Logic_Unit_result), .in1(DMEM_p5), .out(multiplexer_7_out), .sel(MemtoReg));

  // Other names for the same wires on the sheet: clk = CLOCK

  // Notes on the sheet:
  //   Output
  //   IMEM (do **NOT** move this)
  //   Inputs
  //   Inputs/Outputs for testing. Do **NOT** move these.
  //   It is OK to move the PC, RegFile, ALU, and MEM to wherever is most convenient for you when constructing your CPU, and to delete this text
endmodule

// immcr
module ImmediateGenerator (
  input  [31:0] INSTRUCTION,
  output [31:0] I,
  output [31:0] S,
  output [31:0] B,
  output [31:0] U,
  output [31:0] J
);

  assign I[31:11] = {{20{INSTRUCTION[31]}}, INSTRUCTION[31]};  // Bit_Extender bit_extender_1
  assign S[31:11] = {{20{INSTRUCTION[31]}}, INSTRUCTION[31]};  // Bit_Extender bit_extender_2
  assign J[31:20] = {{11{INSTRUCTION[31]}}, INSTRUCTION[31]};  // Bit_Extender bit_extender_3
  assign B[31:12] = {{19{INSTRUCTION[31]}}, INSTRUCTION[31]};  // Bit_Extender bit_extender_4

  assign B[11:0] = {INSTRUCTION[7], INSTRUCTION[30:25], INSTRUCTION[11:8], 1'b0};
  assign I[10:0] = INSTRUCTION[30:20];
  assign J[19:0] = {INSTRUCTION[19:12], INSTRUCTION[20], INSTRUCTION[30:21], 1'b0};
  assign S[10:0] = {INSTRUCTION[30:25], INSTRUCTION[11:7]};
  assign U = {INSTRUCTION[31:12], {12{1'b0}}};

  // Other names for the same wires on the sheet: imm5B[4:0] = INSTRUCTION[11:7]; imm5S[4:0] = INSTRUCTION[11:7];
  //   INSTRUCTION0[31:0] = INSTRUCTION; rdI[4:0] = INSTRUCTION[11:7]; rdJ[4:0] = INSTRUCTION[11:7];
  //   rdR[4:0] = INSTRUCTION[11:7]; rdU[4:0] = INSTRUCTION[11:7]; opcodeB[6:0] = INSTRUCTION[6:0];
  //   opcodeI[6:0] = INSTRUCTION[6:0]; opcodeJ[6:0] = INSTRUCTION[6:0]; opcodeR[6:0] = INSTRUCTION[6:0];
  //   opcodeS[6:0] = INSTRUCTION[6:0]; opcodeU[6:0] = INSTRUCTION[6:0]; imm10J[9:0] = INSTRUCTION[30:21];
  //   imm12I[11:0] = INSTRUCTION[31:20]; imm20U[19:0] = INSTRUCTION[31:12]; rs2B[4:0] = INSTRUCTION[24:20];
  //   rs2R[4:0] = INSTRUCTION[24:20]; rs2S[4:0] = INSTRUCTION[24:20]; func7R[6:0] = INSTRUCTION[31:25];
  //   imm7B[6:0] = INSTRUCTION[31:25]; imm7S[6:0] = INSTRUCTION[31:25]; imm01J = INSTRUCTION[20];
  //   func3B[2:0] = INSTRUCTION[14:12]; func3I[2:0] = INSTRUCTION[14:12]; func3R[2:0] = INSTRUCTION[14:12];
  //   func3S[2:0] = INSTRUCTION[14:12]; imm8J[7:0] = INSTRUCTION[19:12]; rs1B[4:0] = INSTRUCTION[19:15];
  //   rs1I[4:0] = INSTRUCTION[19:15]; rs1R[4:0] = INSTRUCTION[19:15]; rs1S[4:0] = INSTRUCTION[19:15];
  //   imm1J = INSTRUCTION[31]
endmodule

module ControlModule (
  input  [6:0] opcode,
  input  [6:0] func7,
  input  [2:0] func3,
  input  zero,
  output ALUsrc,
  output MentoReg,
  output RegWr,
  output MenWr,
  output [2:0] ExtOp,
  output [3:0] ALUctr,
  output nPCsel,
  output jump,
  output [1:0] lhb
);

  wire add, addi, and1, and_33_out, and_34_out, and_35_out, and_36_out, andi, beq, blt, bltu, bne,
       comparator_1_eq, comparator_2_eq, comparator_3_eq, comparator_4_eq, comparator_5_eq, comparator_6_eq,
       comparator_7_eq, ctr0, ctr1, ctr2, ctr3, ctr4, ctr5, ctr6, ctr7, ctr8, ctr9, ctr10, ctr11, ctr12,
       ctr13, ctr14, jal, jar, lb, lh, lw, not_1_out, not_2_out, not_3_out, not_4_out, not_5_out, or1, ori,
       register_1_q, sll1, slli, slt, slti, srl1, srli, sub, xor1, xori;
  wire [2:0] multiplexer_1_out, multiplexer_2_out, multiplexer_3_out, multiplexer_4_out, multiplexer_5_out,
       multiplexer_6_out, multiplexer_7_out;
  wire [3:0] multiplexer_8_out, multiplexer_9_out, multiplexer_10_out, multiplexer_11_out,
       multiplexer_12_out, multiplexer_13_out, multiplexer_14_out, multiplexer_15_out, multiplexer_16_out,
       multiplexer_17_out, multiplexer_18_out, multiplexer_19_out, multiplexer_20_out, multiplexer_21_out;

  Comparator #(.width(7)) comparator_1 (.a(opcode), .b(7'b0000011), .eq(comparator_1_eq));  // open: gt, lt
  Comparator #(.width(7)) comparator_2 (.a(opcode), .b(7'b0010011), .eq(comparator_2_eq));  // open: gt, lt
  Comparator #(.width(7)) comparator_3 (.a(opcode), .b(7'b0100011), .eq(comparator_3_eq));  // open: gt, lt
  Comparator #(.width(7)) comparator_4 (.a(opcode), .b(7'b1100011), .eq(comparator_4_eq));  // open: gt, lt
  Comparator #(.width(7)) comparator_5 (.a(opcode), .b(7'b1100111), .eq(comparator_5_eq));  // open: gt, lt
  Comparator #(.width(7)) comparator_6 (.a(opcode), .b(7'b0110111), .eq(comparator_6_eq));  // open: gt, lt
  Comparator #(.width(7)) comparator_7 (.a(opcode), .b(7'b1101111), .eq(comparator_7_eq));  // open: gt, lt
  Multiplexer #(.width(3), .enable("false")) multiplexer_1 (
    .in0(3'b000), .in1(3'b000), .out(multiplexer_1_out), .sel(comparator_1_eq));
  Multiplexer #(.width(3), .enable("false")) multiplexer_2 (
    .in0(3'b000), .in1(3'b000), .out(multiplexer_2_out), .sel(comparator_2_eq));
  Multiplexer #(.width(3), .enable("false")) multiplexer_3 (
    .in0(3'b000), .in1(3'b001), .out(multiplexer_3_out), .sel(comparator_3_eq));
  Multiplexer #(.width(3), .enable("false")) multiplexer_4 (
    .in0(3'b000), .in1(3'b010), .out(multiplexer_4_out), .sel(comparator_4_eq));
  Multiplexer #(.width(3), .enable("false")) multiplexer_5 (
    .in0(3'b000), .in1(3'b000), .out(multiplexer_5_out), .sel(comparator_5_eq));
  Multiplexer #(.width(3), .enable("false")) multiplexer_6 (
    .in0(3'b000), .in1(3'b011), .out(multiplexer_6_out), .sel(comparator_6_eq));
  Multiplexer #(.width(3), .enable("false")) multiplexer_7 (
    .in0(3'b000), .in1(3'b100), .out(multiplexer_7_out), .sel(comparator_7_eq));
  assign ExtOp = multiplexer_1_out | multiplexer_2_out | multiplexer_3_out | multiplexer_4_out | multiplexer_5_out | multiplexer_6_out | multiplexer_7_out;  // OR_Gate or_1, 3 bits wide
  and and_1 (add, ~opcode[6], opcode[5], opcode[4], ~opcode[3], ~opcode[2], opcode[1], opcode[0], ~func7[6], ~func7[5], ~func7[4], ~func7[3], ~func7[2], ~func7[1], ~func7[0], ~func3[2], ~func3[1], ~func3[0]);  // AND_Gate
  and and_2 (ctr10, ~opcode[6], opcode[5], opcode[4], ~opcode[3], ~opcode[2], opcode[1], opcode[0], ~func7[6], ~func7[5], ~func7[4], ~func7[3], ~func7[2], ~func7[1], func7[0], ~func3[2], ~func3[1], ~func3[0]);  // AND_Gate
  and and_3 (sub, ~opcode[6], opcode[5], opcode[4], ~opcode[3], ~opcode[2], opcode[1], opcode[0], ~func7[6], func7[5], ~func7[4], ~func7[3], ~func7[2], ~func7[1], ~func7[0], ~func3[2], ~func3[1], ~func3[0]);  // AND_Gate
  and and_4 (sll1, ~opcode[6], opcode[5], opcode[4], ~opcode[3], ~opcode[2], opcode[1], opcode[0], ~func7[6], ~func7[5], ~func7[4], ~func7[3], ~func7[2], ~func7[1], ~func7[0], ~func3[2], ~func3[1], func3[0]);  // AND_Gate
  and and_5 (ctr14, ~opcode[6], opcode[5], opcode[4], ~opcode[3], ~opcode[2], opcode[1], opcode[0], ~func7[6], ~func7[5], ~func7[4], ~func7[3], ~func7[2], ~func7[1], func7[0], ~func3[2], ~func3[1], func3[0]);  // AND_Gate
  and and_6 (ctr11, ~opcode[6], opcode[5], opcode[4], ~opcode[3], ~opcode[2], opcode[1], opcode[0], ~func7[6], ~func7[5], ~func7[4], ~func7[3], ~func7[2], ~func7[1], func7[0], ~func3[2], func3[1], func3[0]);  // AND_Gate
  and and_7 (slt, ~opcode[6], opcode[5], opcode[4], ~opcode[3], ~opcode[2], opcode[1], opcode[0], ~func7[6], ~func7[5], ~func7[4], ~func7[3], ~func7[2], ~func7[1], ~func7[0], ~func3[2], func3[1], ~func3[0]);  // AND_Gate
  and and_8 (xor1, ~opcode[6], opcode[5], opcode[4], ~opcode[3], ~opcode[2], opcode[1], opcode[0], ~func7[6], ~func7[5], ~func7[4], ~func7[3], ~func7[2], ~func7[1], ~func7[0], func3[2], ~func3[1], ~func3[0]);  // AND_Gate
  and and_9 (ctr8, ~opcode[6], opcode[5], opcode[4], ~opcode[3], ~opcode[2], opcode[1], opcode[0], ~func7[6], ~func7[5], ~func7[4], ~func7[3], ~func7[2], ~func7[1], func7[0], func3[2], ~func3[1], func3[0]);  // AND_Gate
  and and_10 (srl1, ~opcode[6], opcode[5], opcode[4], ~opcode[3], ~opcode[2], opcode[1], opcode[0], ~func7[6], ~func7[5], ~func7[4], ~func7[3], ~func7[2], ~func7[1], ~func7[0], func3[2], ~func3[1], func3[0]);  // AND_Gate
  and and_11 (or1, ~opcode[6], opcode[5], opcode[4], ~opcode[3], ~opcode[2], opcode[1], opcode[0], ~func7[6], ~func7[5], ~func7[4], ~func7[3], ~func7[2], ~func7[1], ~func7[0], func3[2], func3[1], ~func3[0]);  // AND_Gate
  and and_12 (ctr9, ~opcode[6], opcode[5], opcode[4], ~opcode[3], ~opcode[2], opcode[1], opcode[0], ~func7[6], ~func7[5], ~func7[4], ~func7[3], ~func7[2], ~func7[1], func7[0], func3[2], func3[1], func3[0]);  // AND_Gate
  and and_13 (and1, ~opcode[6], opcode[5], opcode[4], ~opcode[3], ~opcode[2], opcode[1], opcode[0], ~func7[6], ~func7[5], ~func7[4], ~func7[3], ~func7[2], ~func7[1], ~func7[0], func3[2], func3[1], func3[0]);  // AND_Gate
  and and_14 (lb, ~opcode[6], ~opcode[5], ~opcode[4], ~opcode[3], ~opcode[2], opcode[1], opcode[0], ~func3[2], ~func3[1], ~func3[0]);  // AND_Gate
  and and_15 (lh, ~opcode[6], ~opcode[5], ~opcode[4], ~opcode[3], ~opcode[2], opcode[1], opcode[0], ~func3[2], ~func3[1], func3[0]);  // AND_Gate
  and and_16 (lw, ~opcode[6], ~opcode[5], ~opcode[4], ~opcode[3], ~opcode[2], opcode[1], opcode[0], ~func3[2], func3[1], ~func3[0]);  // AND_Gate
  and and_17 (addi, ~opcode[6], ~opcode[5], opcode[4], ~opcode[3], ~opcode[2], opcode[1], opcode[0], ~func3[2], ~func3[1], ~func3[0]);  // AND_Gate
  and and_18 (slli, ~opcode[6], ~opcode[5], opcode[4], ~opcode[3], ~opcode[2], opcode[1], opcode[0], ~func7[6], ~func7[5], ~func7[4], ~func7[3], ~func7[2], ~func7[1], ~func7[0], ~func3[2], ~func3[1], func3[0]);  // AND_Gate
  and and_19 (slti, ~opcode[6], ~opcode[5], opcode[4], ~opcode[3], ~opcode[2], opcode[1], opcode[0], ~func3[2], func3[1], ~func3[0]);  // AND_Gate
  and and_20 (xori, ~opcode[6], ~opcode[5], opcode[4], ~opcode[3], ~opcode[2], opcode[1], opcode[0], func3[2], ~func3[1], ~func3[0]);  // AND_Gate
  and and_21 (srli, ~opcode[6], ~opcode[5], opcode[4], ~opcode[3], ~opcode[2], opcode[1], opcode[0], ~func7[6], ~func7[5], ~func7[4], ~func7[3], ~func7[2], ~func7[1], ~func7[0], func3[2], ~func3[1], func3[0]);  // AND_Gate
  and and_22 (ctr5, ~opcode[6], ~opcode[5], opcode[4], ~opcode[3], ~opcode[2], opcode[1], opcode[0], ~func7[6], func7[5], ~func7[4], ~func7[3], ~func7[2], ~func7[1], ~func7[0], func3[2], ~func3[1], func3[0]);  // AND_Gate
  and and_23 (ori, ~opcode[6], ~opcode[5], opcode[4], ~opcode[3], ~opcode[2], opcode[1], opcode[0], func3[2], func3[1], ~func3[0]);  // AND_Gate
  and and_24 (jar, opcode[6], opcode[5], ~opcode[4], ~opcode[3], opcode[2], opcode[1], opcode[0], ~func3[2], ~func3[1], ~func3[0]);  // AND_Gate
  and and_25 (andi, ~opcode[6], ~opcode[5], opcode[4], ~opcode[3], ~opcode[2], opcode[1], opcode[0], func3[2], func3[1], func3[0]);  // AND_Gate
  and and_26 (MenWr, ~opcode[6], opcode[5], ~opcode[4], ~opcode[3], ~opcode[2], opcode[1], opcode[0], ~func3[2], func3[1], ~func3[0]);  // AND_Gate
  and and_27 (beq, opcode[6], opcode[5], ~opcode[4], ~opcode[3], ~opcode[2], opcode[1], opcode[0], ~func3[2], ~func3[1], ~func3[0]);  // AND_Gate
  and and_28 (blt, opcode[6], opcode[5], ~opcode[4], ~opcode[3], ~opcode[2], opcode[1], opcode[0], func3[2], ~func3[1], ~func3[0]);  // AND_Gate
  and and_29 (bltu, opcode[6], opcode[5], ~opcode[4], ~opcode[3], ~opcode[2], opcode[1], opcode[0], func3[2], func3[1], ~func3[0]);  // AND_Gate
  and and_30 (bne, opcode[6], opcode[5], ~opcode[4], ~opcode[3], ~opcode[2], opcode[1], opcode[0], ~func3[2], ~func3[1], func3[0]);  // AND_Gate
  and and_31 (ctr13, ~opcode[6], opcode[5], opcode[4], ~opcode[3], opcode[2], opcode[1], opcode[0]);  // AND_Gate
  and and_32 (jal, opcode[6], opcode[5], ~opcode[4], opcode[3], opcode[2], opcode[1], opcode[0]);  // AND_Gate
  Multiplexer #(.width(4), .enable("false")) multiplexer_8 (
    .in0(4'b0000), .in1(4'b0000), .out(multiplexer_8_out), .sel(ctr0));
  Multiplexer #(.width(4), .enable("false")) multiplexer_9 (
    .in0(multiplexer_8_out), .in1(4'b0001), .out(multiplexer_9_out), .sel(ctr1));
  Multiplexer #(.width(4), .enable("false")) multiplexer_10 (
    .in0(multiplexer_9_out), .in1(4'b0010), .out(multiplexer_10_out), .sel(ctr2));
  Register #(.width(1)) register_1 (.D(bne), .Q(register_1_q));  // open: en, clk, clr
  Multiplexer #(.width(4), .enable("false")) multiplexer_11 (
    .in0(multiplexer_10_out), .in1(4'b0011), .out(multiplexer_11_out), .sel(ctr3));
  Multiplexer #(.width(4), .enable("false")) multiplexer_12 (
    .in0(multiplexer_11_out), .in1(4'b0100), .out(multiplexer_12_out), .sel(ctr4));
  and and_33 (and_33_out, zero, beq);
  not not_1 (not_1_out, zero);
  and and_34 (and_34_out, not_1_out, register_1_q);
  and and_35 (and_35_out, blt, not_2_out);
  not not_2 (not_2_out, zero);
  not not_3 (not_3_out, zero);
  Multiplexer #(.width(4), .enable("false")) multiplexer_13 (
    .in0(multiplexer_12_out), .in1(4'b0101), .out(multiplexer_13_out), .sel(ctr5));
  or or_2 (nPCsel, and_33_out, and_34_out, and_35_out, and_36_out);
  and and_36 (and_36_out, not_3_out, bltu);
  Multiplexer #(.width(4), .enable("false")) multiplexer_14 (
    .in0(multiplexer_13_out), .in1(4'b0110), .out(multiplexer_14_out), .sel(ctr6));
  Multiplexer #(.width(4), .enable("false")) multiplexer_15 (
    .in0(multiplexer_14_out), .in1(4'b0111), .out(multiplexer_15_out), .sel(ctr7));
  Multiplexer #(.width(4), .enable("false")) multiplexer_16 (
    .in0(multiplexer_15_out), .in1(4'b1000), .out(multiplexer_16_out), .sel(ctr8));
  not not_4 (not_4_out, lb);
  not not_5 (not_5_out, lh);
  Multiplexer #(.width(4), .enable("false")) multiplexer_17 (
    .in0(multiplexer_16_out), .in1(4'b1001), .out(multiplexer_17_out), .sel(ctr9));
  or or_3 (jump, jar, jal);
  and and_37 (lhb[0], lb, not_5_out);
  and and_38 (lhb[1], lh, not_4_out);
  Multiplexer #(.width(4), .enable("false")) multiplexer_18 (
    .in0(multiplexer_17_out), .in1(4'b1010), .out(multiplexer_18_out), .sel(ctr10));
  Multiplexer #(.width(4), .enable("false")) multiplexer_19 (
    .in0(multiplexer_18_out), .in1(4'b1011), .out(multiplexer_19_out), .sel(ctr11));
  Multiplexer #(.width(4), .enable("false")) multiplexer_20 (
    .in0(multiplexer_19_out), .in1(4'b1100), .out(multiplexer_20_out), .sel(ctr12));
  or or_4 (MentoReg, lb, lh, lw);
  or or_5 (RegWr, add, ctr10, sub, sll1, ctr14, ctr11, slt, xor1, ctr8, srl1, or1, ctr9, and1, lb, lh, lw, addi, slli, slti, xori, srli, ctr5, ori, jar, andi, ctr13, jal);
  Multiplexer #(.width(4), .enable("false")) multiplexer_21 (
    .in0(multiplexer_20_out), .in1(4'b1101), .out(multiplexer_21_out), .sel(ctr13));
  or or_6 (ALUsrc, lb, lh, lw, addi, slli, slti, xori, srli, ctr5, ori, jar, andi, MenWr, ctr13, jal);
  or or_7 (ctr0, add, lb, lh, lw, addi, jar, MenWr, jal);
  or or_8 (ctr1, and1, andi);
  or or_9 (ctr2, or1, ori);
  or or_10 (ctr3, xor1, xori);
  or or_11 (ctr4, srl1, srli);
  or or_12 (ctr6, sll1, slli);
  or or_13 (ctr7, slt, slti, blt, bltu);
  or or_14 (ctr12, sub, beq, bne);
  Multiplexer #(.width(4), .enable("false")) multiplexer_22 (
    .in0(multiplexer_21_out), .in1(4'b1110), .out(ALUctr), .sel(ctr14));

  // Other names for the same wires on the sheet: divu = ctr8; lui = ctr13; mul = ctr10; mulh = ctr14; mulhu = ctr11;
  //   remu = ctr9; srai = ctr5; sw = MenWr
endmodule

module load (
  input  [31:0] in_1,
  input  [1:0] in_2,
  output [31:0] out_3
);

  wire [31:0] bit_extender_1_out, bit_extender_2_out;

  assign bit_extender_1_out = {{16{in_1[15]}}, in_1[15:0]};  // Bit_Extender bit_extender_1
  assign bit_extender_2_out = {{24{in_1[7]}}, in_1[7:0]};  // Bit_Extender bit_extender_2
  Multiplexer #(.select(2), .width(32), .enable("false")) multiplexer_1 (
    .in0(in_1), .in1(bit_extender_2_out), .in2(bit_extender_1_out), .out(out_3), .sel(in_2));  // open: in3
endmodule
